# Fritzing sketch diagram (saved by Fritzing 0.9.10b)

parts:
  LCD2004-I2C1 = LCD2004-I2C
  ZS-042_RTC1 = ZS-042 RTC Module
  microSD1 = MicroSD Card Module
  BAT2 = 18650 battery holder [package=battery-18650-kit]
  BAT3 = 18650 battery holder [package=battery-18650-kit]
  Mod1 = Voltage Sensor 25V
  J2 = female pin header, 2 pins [form="♀ (female)"]
  J3 = female pin header, 2 pins [form="♀ (female)"]
  J7 = female pin header, 2 pins [form="♀ (female)"]
  Part3 = Arduino Mega 2560 (Rev3)
  J8 = female pin header, 2 pins [form="♀ (female)"]
  8_Channel_Relay1 = 8 Channel Power Relay
  J9 = female pin header, 2 pins [form="♀ (female)"]
  T1 = LM35 Temperature Sensor [package="TO92 [THT]"]
  T2 = LM35 Temperature Sensor [package="TO92 [THT]"]
  T3 = LM35 Temperature Sensor [package="TO92 [THT]"]
  R1 = Resistor [tolerance=±5% resistance=220 package="2010 [SMD]"]
  J12 = Dagu DGServo 9g header (male) [package=THT]
  J13 = Dagu DGServo 9g header (male) [package=THT]
  J14 = Dagu DGServo 9g header (male) [package=THT]
  J15 = female pin header, 2 pins [form="♀ (female)"]
  Mod2 = 3S-BMS
  BAT1 = 18650 battery holder [package=battery-18650-kit]
  A1 = j5019
  U1 = LIPO-110mAh [package=lipo-110]
  J16 = Power Jack [package=power_jack_combo]

nets:
  N1: LCD2004-I2C1.GND, J2.pin1
  N2: LCD2004-I2C1.VCC, J2.pin2
  N3: LCD2004-I2C1.SDA, ZS-042_RTC1.SDA, Part3.D20/SDA
  N4: LCD2004-I2C1.SCL, ZS-042_RTC1.SCL, Part3.D21/SCL
  N5: ZS-042_RTC1.GND, J3.pin1
  N6: ZS-042_RTC1.VCC, J3.pin2
  N7: microSD1.GND, J8.pin1
  N8: microSD1.VCC, J8.pin2
  N9: microSD1.MISO, Part3.D48
  N10: microSD1.MOSI, Part3.D49
  N11: microSD1.SCK, Part3.D50
  N12: microSD1.CS, Part3.D51
  N13: BAT2.+, 8_Channel_Relay1.COM#31, 8_Channel_Relay1.COM#34, Mod2.8.4V, BAT1.-
  N14: BAT2.-, BAT3.+, 8_Channel_Relay1.COM#25, 8_Channel_Relay1.COM#28
  N15: BAT3.-, 8_Channel_Relay1.COM#22, Mod2.0V
  N16: Mod1.GND, Mod1.-, J7.pin2, 8_Channel_Relay1.NO#23, 8_Channel_Relay1.NO#29, 8_Channel_Relay1.NO#35
  N17: Mod1.VCC, 8_Channel_Relay1.NC, R1.Pin_1
  N18: Mod1.S, Part3.A0
  N19: Mod1.+, J7.pin1
  N20: Part3.A1, T1.Vout, J12.Vcc
  N21: Part3.A2, T2.Vout, J13.Vcc
  N22: Part3.A3, T3.Vout, J14.Vcc
  N23: Part3.GND, A1.Pin_2, A1.Pin_4, A1.Pin_5, U1.-, J16.GNDBREAK
  N24: Part3.VIN, A1.Pin_1
  N25: Part3.D30, 8_Channel_Relay1.IN1
  N26: Part3.D31, 8_Channel_Relay1.IN2
  N27: Part3.D32, 8_Channel_Relay1.IN3
  N28: Part3.D33, 8_Channel_Relay1.IN4
  N29: Part3.D34, 8_Channel_Relay1.IN5
  N30: Part3.D35, 8_Channel_Relay1.IN6
  N31: Part3.D36, 8_Channel_Relay1.IN7
  N32: Part3.D37, 8_Channel_Relay1.IN8
  N33: 8_Channel_Relay1.GND, J9.pin1
  N34: 8_Channel_Relay1.VCC, J9.pin2
  N35: 8_Channel_Relay1.NO#26, 8_Channel_Relay1.NO#32, 8_Channel_Relay1.NO#38, 8_Channel_Relay1.COM#40
  N36: 8_Channel_Relay1.COM#37, Mod2.12.6V, BAT1.+
  N37: 8_Channel_Relay1.NO#41, R1.Pin_0
  N38: T1.+Vs, T2.+Vs, T3.+Vs, J12.pulse, J13.pulse, J14.pulse, J15.pin2
  GND: T1.GND, T2.GND, T3.GND, J12.gnd, J13.gnd, J14.gnd, J15.pin1
  N39: A1.Pin_3, J16.PWR
  N40: A1.Pin_6, U1.+

custom parts:
  LCD2004-I2C: A standard character display with 4x20 characters. Comes in many colors with LCM2004 IIC attached.
  18650 battery holder: 18650 Battery Holder
  8 Channel Power Relay: An 8 channel power relay. The module operates at 5V.
  3S-BMS: 3S-BMS LIPO battery charger / protection unit. Note pcb does not match the board as it will likely connect with wires, so pcb is 6 pads suitable for .1in header pins.
  j5019: This module is a small single cell lithium battery charging module which also includes a 1A step-up (boost) converter for powering a large range of applications.
